// Logisim project ex4.circ as structural Verilog: 1 circuit, main circuit Split
module Split (
  input  [7:0] In1,
  output Out1,
  output [7:0] Out2
);

  and and_1 (Out1, In1[0], In1[7]);
  not not_1 (Out2[0], In1[0]);

  assign Out2[7:1] = In1[7:1];

  // Notes on the sheet:
  //   PUT CIRCUITRY HERE
endmodule
