// Logisim project ex5.circ as structural Verilog: 5 circuits, main circuit rotr
module rotr (
  input  [15:0] A,
  input  [3:0] B,
  output [15:0] Out1
);

  wire [15:0] rot1_1_out_3, rot2_1_out_3, rot4_1_out_3;

  rot1 rot1_1 (.input_A(A), .input_B_0(B[0]), .out_3(rot1_1_out_3));
  rot2 rot2_1 (.input_A(rot1_1_out_3), .input_B_1(B[1]), .out_3(rot2_1_out_3));
  rot4 rot4_1 (.input_A(rot2_1_out_3), .input_B_2(B[2]), .out_3(rot4_1_out_3));
  rot8 rot8_1 (.input_A(rot4_1_out_3), .input_B_3(B[3]), .out_3(Out1));

  // Notes on the sheet:
  //   PUT CIRCUITRY HERE
endmodule

module rot8 (
  input  [15:0] input_A,
  input  input_B_3,
  output [15:0] out_3
);

  Multiplexer #(.enable("false"), .width(16)) multiplexer_1 (
    .in0(input_A), .in1({input_A[7:0], input_A[15:8]}), .out(out_3), .sel(input_B_3));

  // Notes on the sheet:
  //   PUT CIRCUITRY HERE
endmodule

module rot4 (
  input  [15:0] input_A,
  input  input_B_2,
  output [15:0] out_3
);

  Multiplexer #(.enable("false"), .width(16)) multiplexer_1 (
    .in0(input_A), .in1({input_A[3:0], input_A[15:4]}), .out(out_3), .sel(input_B_2));

  // Notes on the sheet:
  //   PUT CIRCUITRY HERE
endmodule

module rot2 (
  input  [15:0] input_A,
  input  input_B_1,
  output [15:0] out_3
);

  Multiplexer #(.enable("false"), .width(16)) multiplexer_1 (
    .in0(input_A), .in1({input_A[1:0], input_A[15:2]}), .out(out_3), .sel(input_B_1));

  // Notes on the sheet:
  //   PUT CIRCUITRY HERE
endmodule

module rot1 (
  input  [15:0] input_A,
  input  input_B_0,
  output [15:0] out_3
);

  Multiplexer #(.enable("false"), .width(16)) multiplexer_1 (
    .in0(input_A), .in1({input_A[0], input_A[15:1]}), .out(out_3), .sel(input_B_0));

  // Notes on the sheet:
  //   PUT CIRCUITRY HERE
endmodule
